# Fritzing sketch c (saved by Fritzing 0.9.4)
breadboards: 1

parts:
  Power_plug1 = Power plug
  U1 = 555 Timer [package="DIP8 [THT]"]
  C1 = Capacitor [package=cap-pth-small]
  C2 = Capacitor [package=cap-pth-small]
  R1 = 12 kΩ Resistor [package=THT]
  R3 = Rotary Potentiometer (Large) [maximum_resistance=100kΩ package=THT]
  R2 = 1.5 kΩ Resistor [package=THT]

nets:
  N1: Power_plug1.GND, U1.Ground, C1.1, C2.2
  N2: Power_plug1.VCC, U1.Reset, U1.Vcc_Supply_Voltage, R3.wiper
  N3: U1.Trigger, U1.Threshold, C1.2, R2.Pin_0
  N4: U1.Control_Voltage, C2.1
  N5: U1.Discharge, R1.Pin_0, R2.Pin_1
  N6: R1.Pin_1, R3.leg1

notes:
  V output

custom parts:
  12 kΩ Resistor: A generic resistor (0.25W)
  1.5 kΩ Resistor: A generic resistor (0.25W)
