# Fritzing sketch d (saved by Fritzing 0.9.4)
breadboards: 1

parts:
  Power_plug1 = Power plug
  U1 = 555 Timer [package="DIP8 [THT]"]
  C1 = Capacitor [package=cap-pth-small]
  C2 = Capacitor [package=cap-pth-small]
  R1 = 1.5 kΩ Resistor [package=THT]
  R2 = 1.5 kΩ Resistor [package=THT]
  74HC1 = DIP - 14 pins [chip_label=74HC04 package="DIP (Dual Inline) [THT]"]

nets:
  N1: Power_plug1.GND, U1.Ground, C1.1, C2.2, 74HC1.pin7
  N2: Power_plug1.VCC, U1.Reset, U1.Vcc_Supply_Voltage, R2.Pin_1, 74HC1.pin14
  N3: U1.Trigger, U1.Threshold, C1.2, R1.Pin_0
  N4: U1.Output, 74HC1.pin1
  N5: U1.Control_Voltage, C2.1
  N6: U1.Discharge, R1.Pin_1, R2.Pin_0

notes:
  V output

custom parts:
  1.5 kΩ Resistor: A generic resistor (0.25W)
  DIP - 14 pins: A DIP stand-in part for whatever IC you want. With 14 pins on a 300mil dual inline package (DIP) footprint.
