# Fritzing sketch a (saved by Fritzing 0.9.10b)
breadboards: 2

parts:
  R1 = Resistor [tolerance=±5% resistance=220 power=0.25 package=THT]
  R2 = Resistor [tolerance=±5% resistance=220 power=0.25 package=THT]
  S1 = Toggle Switch [package=THT]
  S2 = Toggle Switch [package=THT]
  IC2 = IC, DIP package, 16 pins [chip_label=IC74173(D-FF)]
  IC4 = IC, DIP package, 16 pins [chip_label=IC74153(mux)]
  IC3 = IC, DIP package, 16 pins [chip_label=IC74153(mux)]
  Power_plug1 = Power plug

nets:
  N1: R1.Pin_0, R2.Pin_0, IC2.pin16, IC4.pin16, IC3.pin16, Power_plug1.VCC
  N2: R1.Pin_1, S2.COM, IC4.pin14, IC3.pin14
  N3: R2.Pin_1, S1.COM, IC3.pin6
  N4: S1.L2, S2.L2, IC2.pin8, IC4.pin8, IC3.pin8, Power_plug1.GND
  N5: IC2.pin3, IC3.pin10
  N6: IC2.pin4, IC4.pin6
  N7: IC2.pin5, IC4.pin10
  N8: IC2.pin11, IC4.pin9
  N9: IC2.pin12, IC4.pin7
  N10: IC2.pin13, IC3.pin9
  N11: IC2.pin14, IC3.pin7

notes:
  Clock
  PE not
  PE
  A B C D
