# Fritzing sketch d (saved by Fritzing 0.9.4)
breadboards: 2

parts:
  R1 = Resistor [tolerance=±5% resistance=220 package=THT]
  R2 = Resistor [tolerance=±5% resistance=220 package=THT]
  VCC1 = 4 x AAA Battery Mount
  S1 = Toggle Switch [package=THT]
  S2 = Toggle Switch [package=THT]
  IC2 = IC, DIP package, 16 pins [chip_label=IC74173(D-FF)]
  IC4 = IC, DIP package, 16 pins [chip_label=IC74153(mux)]
  IC3 = IC, DIP package, 16 pins [chip_label=IC74153(mux)]
  IC5 = IC, DIP package, 14 pins [chip_label=IC7404(not)]

nets:
  N1: R1.Pin_0, R2.Pin_0, VCC1.+, IC2.pin16, IC4.pin16, IC3.pin16, IC5.pin14
  N2: R1.Pin_1, S2.COM, IC4.pin14, IC3.pin14
  N3: R2.Pin_1, S1.COM
  N4: VCC1.-, S1.L2, S2.L2, IC2.pin8, IC4.pin8, IC3.pin8, IC5.pin7
  N5: IC2.pin3, IC3.pin10
  N6: IC2.pin4, IC4.pin6
  N7: IC2.pin5, IC4.pin10
  N8: IC2.pin6, IC5.pin1
  N9: IC2.pin11, IC4.pin9
  N10: IC2.pin12, IC4.pin7
  N11: IC2.pin13, IC3.pin9
  N12: IC2.pin14, IC3.pin7
  N13: IC3.pin6, IC5.pin2

notes:
  clock
  PE not
  PE
  A B C D
