# Fritzing sketch f (saved by Fritzing 0.9.4)
breadboards: 1

parts:
  IC1 = IC, DIP package, 14 pins [chip_label=IC7495]
  VCC1 = 4 x AAA Battery Mount

nets:
  N1: IC1.pin3, IC1.pin13
  N2: IC1.pin4, IC1.pin12
  N3: IC1.pin5, IC1.pin11
  N4: IC1.pin7, VCC1.-
  N5: IC1.pin14, VCC1.+

notes:
  clock
  in
