# Fritzing sketch g (saved by Fritzing 0.9.4)
breadboards: 2

parts:
  IC1 = IC, DIP package, 14 pins [chip_label=IC7495]
  IC2 = IC, DIP package, 14 pins [chip_label=IC7432(or)]
  IC3 = IC, DIP package, 14 pins [chip_label=IC7408(and)]
  IC4 = IC, DIP package, 14 pins [chip_label=IC7404(not)]
  R1 = Resistor [tolerance=±5% resistance=220 package=THT]
  R2 = Resistor [tolerance=±5% resistance=220 package=THT]
  VCC1 = 4 x AAA Battery Mount
  S1 = Toggle Switch [package=THT]
  S2 = Toggle Switch [package=THT]
  IC5 = IC, DIP package, 14 pins [chip_label=IC7408(and)]

nets:
  N1: IC1.pin7, IC2.pin7, IC3.pin7, IC4.pin7, VCC1.-, S1.L2, S2.L2, IC5.pin7
  N2: IC1.pin8, IC1.pin9
  N3: IC1.pin14, IC2.pin14, IC3.pin14, IC4.pin14, R1.Pin_0, R2.Pin_0, VCC1.+, IC5.pin14
  N4: IC2.pin1, IC3.pin6
  N5: IC2.pin2, IC3.pin3
  N6: IC2.pin4, IC5.pin3
  N7: IC2.pin5, IC5.pin6
  N8: IC2.pin9, IC5.pin8
  N9: IC2.pin10, IC5.pin11
  N10: IC2.pin12, IC3.pin11
  N11: IC2.pin13, IC3.pin8
  N12: IC4.pin13, R1.Pin_1, S2.COM
  N13: R2.Pin_1, S1.COM

notes:
  PE not
  PE
