# Fritzing sketch gussy (saved by Fritzing 0.9.4)
breadboards: 2

parts:
  R1 = Resistor [tolerance=±5% resistance=220 package=THT]
  R2 = Resistor [tolerance=±5% resistance=220 package=THT]
  VCC1 = 4 x AAA Battery Mount
  S1 = Toggle Switch [package=THT]
  S2 = Toggle Switch [package=THT]
  IC2 = IC, DIP package, 16 pins [chip_label=IC74173(D-FF)]
  IC4 = IC, DIP package, 16 pins [chip_label=IC74153(mux)]
  IC3 = IC, DIP package, 16 pins [chip_label=IC74153(mux)]

nets:
  N1: R1.Pin_0, R2.Pin_0, VCC1.+, IC2.pin16, IC4.pin16, IC3.pin16
  N2: R1.Pin_1, S2.COM, IC3.pin14
  N3: R2.Pin_1, S1.COM
  N4: VCC1.-, S1.L2, S2.L2, IC2.pin8, IC4.pin8, IC3.pin8

notes:
  clock
  PE not
  PE
