# Fritzing sketch h (saved by Fritzing 0.9.4)
breadboards: 1

parts:
  VCC1 = 4 x AAA Battery Mount
  IC1 = IC, DIP package, 24 pins [chip_label=IC74154]
  IC2 = IC, DIP package, 14 pins [chip_label=IC7432(or)]

nets:
  N1: VCC1.-, IC1.pin12, IC2.pin7
  N2: VCC1.+, IC1.pin24, IC2.pin14
  N3: IC1.pin2, IC2.pin1
  N4: IC1.pin3, IC2.pin2
  N5: IC1.pin15, IC2.pin13
  N6: IC1.pin16, IC2.pin12
  N7: IC2.pin3, IC2.pin4
  N8: IC2.pin5, IC2.pin11

notes:
  ABCD
  output
