# Fritzing sketch A (saved by Fritzing 0.9.10b)
breadboards: 1

parts:
  Power_plug1 = Power plug
  IC1 = 74LS109 [chip_label=74LS109 package="DIP (Dual Inline) [THT]"]
  IC2 = 74LS109 [chip_label=74LS109 package="DIP (Dual Inline) [THT]"]
  IC3 = 74HC157 [chip_label=74HC157 package="DIP (Dual Inline) [THT]"]

nets:
  N1: Power_plug1.GND, IC1.pin3, IC1.pin8, IC1.pin13, IC2.pin3, IC2.pin8, IC2.pin13, IC3.pin8
  N2: Power_plug1.VCC, IC1.pin2, IC1.pin14, IC1.pin16, IC2.pin2, IC2.pin14, IC2.pin16, IC3.pin16
  N3: IC1.pin6, IC3.pin2
  N4: IC1.pin7, IC3.pin3
  N5: IC1.pin9, IC3.pin13
  N6: IC1.pin10, IC3.pin14
  N7: IC1.pin12, IC3.pin7
  N8: IC2.pin4, IC3.pin4
  N9: IC2.pin6, IC3.pin5
  N10: IC2.pin7, IC3.pin6
  N11: IC2.pin12, IC3.pin12

notes:
  Select
  Clock

custom parts:
  74LS109: Dual JKFF With Preset and Clear
  74HC157: Quad 2-input Multiplexer
