# Fritzing sketch C (saved by Fritzing 0.9.10b)
breadboards: 1

parts:
  Power_plug1 = Power plug
  74LS1 = 74LS90 [chip_label=74LS90 package="DIP (Dual Inline) [THT]"]
  74LS2 = 74LS90 [chip_label=74LS90 package="DIP (Dual Inline) [THT]"]
  74LS3 = 74LS21 [chip_label=74LS21 package="DIP (Dual Inline) [THT]"]

nets:
  N1: Power_plug1.GND, 74LS1.pin6, 74LS1.pin7, 74LS1.pin10, 74LS2.pin6, 74LS2.pin7, 74LS2.pin10, 74LS3.pin7
  N2: Power_plug1.VCC, 74LS1.pin5, 74LS2.pin5, 74LS3.pin14
  N3: 74LS1.pin1, 74LS1.pin12, 74LS3.pin1
  N4: 74LS1.pin2, 74LS2.pin2, 74LS2.pin3, 74LS3.pin6
  N5: 74LS1.pin9, 74LS3.pin2
  N6: 74LS1.pin11, 74LS2.pin14
  N7: 74LS2.pin1, 74LS2.pin12
  N8: 74LS2.pin8, 74LS3.pin5
  N9: 74LS2.pin9, 74LS3.pin4

notes:
  Q3Q2Q1Q0
  CLOCK

custom parts:
  74LS90: Decade Counter
  74LS21: Two 4-input AND
