# Fritzing sketch D (saved by Fritzing 0.9.4)
breadboards: 1

parts:
  Power_plug1 = Power plug
  74LS1 = 74LS107 [chip_label=74LS107 package="DIP (Dual Inline) [THT]"]
  74LS2 = 74LS107 [chip_label=74LS107 package="DIP (Dual Inline) [THT]"]
  74HC1 = 74HC08 [chip_label=74HC08 package="DIP (Dual Inline) [THT]"]
  74LS3 = 74LS04 [chip_label=74LS04 package="DIP (Dual Inline) [THT]"]
  74LS4 = 74LS32 [chip_label=74LS32 package="DIP (Dual Inline) [THT]"]
  74LS5 = 74LS86 [chip_label=74LS86 package="DIP (Dual Inline) [THT]"]

nets:
  N1: Power_plug1.GND, 74LS1.pin7, 74LS2.pin7, 74HC1.pin7, 74LS3.pin7, 74LS4.pin7, 74LS5.pin7
  N2: Power_plug1.VCC, 74LS1.pin10, 74LS1.pin13, 74LS1.pin14, 74LS2.pin1, 74LS2.pin4, 74LS2.pin13, 74LS2.pin14, 74HC1.pin14, 74LS3.pin14, 74LS4.pin14, 74LS5.pin14
  N3: 74LS1.pin1, 74LS1.pin4, 74LS4.pin6
  N4: 74LS1.pin5, 74HC1.pin9
  N5: 74LS1.pin8, 74LS1.pin11, 74LS5.pin3
  N6: 74LS1.pin9, 74LS1.pin12, 74LS2.pin12
  N7: 74LS2.pin2, 74HC1.pin5
  N8: 74HC1.pin3, 74LS4.pin1
  N9: 74HC1.pin4, 74LS3.pin2
  N10: 74HC1.pin6, 74LS4.pin2
  N11: 74HC1.pin8, 74LS4.pin5
  N12: 74HC1.pin10, 74LS3.pin1
  N13: 74LS4.pin3, 74LS4.pin4

notes:
  CLOCK
  X
  Q2Q1Q0

custom parts:
  74LS107: Dual JK Flip Flop With Clear
  74HC08: Four 2-input AND
  74LS04: Hex Inverter
  74LS32: Quad 2-input OR
  74LS86: Four 2-input XOR
